# Fritzing sketch denahKabel (saved by Fritzing 0.9.6b)

parts:
  U1 = NodeMCU V1.0
  Part1 = RFID-RC522-v2
  Button_led_merah = Round Pushbutton
  J1 = Piezo Speaker
  ZS-042_RTC1 = ZS-042 RTC Module
  Button_led_hijau = Round Pushbutton

nets:
  N1: U1.D1, ZS-042_RTC1.SCL
  N2: U1.D2, ZS-042_RTC1.SDA
  N3: U1.D3, Part1.RST
  N4: U1.D4, Part1.SDA
  3V3: U1.3V3, Part1.3.3V, ZS-042_RTC1.VCC
  N5: U1.D5, Part1.SCK
  N6: U1.D6, Part1.MISO
  N7: U1.D7, Part1.MOSI
  N8: U1.D8, Button_led_merah.leg0, J1.pin1
  GND: U1.GND, Part1.GND, Button_led_merah.leg1, J1.pin2, ZS-042_RTC1.GND, Button_led_hijau.leg1

custom parts:
  NodeMCU V1.0: ESP8266 based NodeMCU
  RFID-RC522-v2: A simple China made RFID-RC522 Reader; do check the pin labels, as this is a MFRC522 based clone.

// code stored in the sketch: denahKabel.ino
#include <Adafruit_LiquidCrystal.h>



//#include <ESP8266HttpClient.h>
//#include <SerialESP8266wifi.h>
#include <WiFiClient.h>
#include <ESP8266WiFi.h>
#include <WiFiClient.h> 
#include <ESP8266HTTPClient.h>
#include <ArduinoJson.h>        // version 6.13
#include <SPI.h>
#include <RFID.h>
#include <Wire.h> 
#include <LiquidCrystal_I2C.h>
#include <RTClib.h>

WiFiClient wifiClient;

RTC_DS3231 rtc;
 
char t [32];
LiquidCrystal_I2C lcd(0x27, 20, 4);       // sesuaikan alamat i2c (0x27) dengan alamat i2c kalian

#define SS_PIN D4
#define RST_PIN D3
#define Buzzer D8
#define lampu D0

//const char* wifiName = "SAINTEK AREA";
//const char* wifiPass = "gosaintek";

//const char* wifiName = "wifi-premium";
//const char* wifiPass = "tanyasayyidul";

const char* wifiName = "CLOSED";
const char* wifiPass = "123Cl0sed321";

//const char* wifiName = "Lab Komputasi Dasar";
//const char* wifiPass = "AKREDITASI2022";

const String iddev = "98";

String hostMode = "http://absensi.xyz/api/getmodejson?key=mrRkmgf82kjrJNkVYjsfnxz&iddev=" + iddev;
String hostSCAN = "http://172.20.20.7:3015/rfid/";
String hostADD = "http://172.20.20.7:3015/rfid/";

//String hostMode = "http://absensi.xyz/api/getmodejson?key=mrRkmgf82kjrJNkVYjsfnxz&iddev=" + iddev;
//String hostSCAN = "http://172.20.20.7:3015/rfid/api/input/db";
//String hostADD = "http://172.20.20.7:3015/rfid/api/input/db";


//String hostMode = "http://absensi.xyz/api/getmodejson?key=mrRkmgf82kjrJNkVYjsfnxz&iddev=" + iddev;
//String hostSCAN = "http://172.20.20.7:3015/smcard/perizinan/keluar";
//String hostADD = "http://172.20.20.7:3015/smcard/perizinan/keluar";


//String hostMode = "http://absensi.xyz/api/getmodejson?key=mrRkmgf82kjrJNkVYjsfnxz&iddev=" + iddev;
//String hostSCAN = "http://172.20.20.7:3015/smcard/perizinan/masuk";
//String hostADD = "http://172.20.20.7:3015/smcard/perizinan/masuk";


String ModeAlat = "";

RFID rfid(SS_PIN, RST_PIN);

void setup() {
  Serial.begin(115200);
  Wire.begin(5, 4);   //Setting wire (5 untuk SDA dan 4 untuk SCL)
   //rtc.begin();
   //rtc.adjust(DateTime(F(DATE),F(TIME)));  //Setting Time

   rtc.begin();
   rtc.adjust(DateTime(F(__DATE__),F(__TIME__)));  //Setting Time
  
  
  //SPI.begin();
  //rfid PCD_Init();
  Serial.print("MASJID");
  Serial.print("");
  
  // Kalian dapat menambahkan bagian dibawah ini untuk set manual jam
  // rtc.adjust(DateTime(2014, 1, 21, 3, 0, 0));
  SPI.begin();
  rfid.init();
  delay(10);

  pinMode(Buzzer, OUTPUT);
  pinMode(lampu, OUTPUT);
  
  Wire.begin(D2,D1);
  //lcd.begin();
  //lcd.home ();
  //lcd.print("RFID Reader Absensi");  
  delay (1000);
  Serial.println();
  
  Serial.print("Connecting to ");
  Serial.println(wifiName);

  lcd.setCursor(0,1);
  lcd.print("Connecting to");
  lcd.setCursor(0,2);
  lcd.print(wifiName);  

  WiFi.begin(wifiName, wifiPass);

  while (WiFi.status() != WL_CONNECTED) {
    delay(500);
    Serial.print(".");
  }

  Serial.println("");
  Serial.println("WiFi connected");
  Serial.println("IP address: ");
  Serial.println(WiFi.localIP());   //You can get IP address assigned to ESP

  ModeDevice();
}

void ModeDevice(){
  HTTPClient http;

  Serial.print("Request Link:");
  Serial.println(hostMode);
  
  http.begin(wifiClient, hostMode);
  
  int httpCode = http.GET();            //Send the request
  String payload = http.getString();    //Get the response payload from server

  Serial.print("Response Code:"); //200 is OK
  Serial.println(httpCode);       //Print HTTP return code

  Serial.print("MASJID");
  Serial.print("");

  Serial.print("Returned data from Server:");
  Serial.println(payload);    //Print request response payload
  
  if(httpCode == 200)
  {
    DynamicJsonDocument doc(1024);
  
   // Parse JSON object
    auto error = deserializeJson(doc, payload);
    if (error) {
      Serial.print(F("deserializeJson() failed with code "));
      Serial.println(error.c_str());
      return;
    }
  
    // Decode JSON/Extract values
    String responStatus = doc["status"].as<String>();
    String responMode = doc["mode"].as<String>();
    String responKet = doc["ket"].as<String>();

    Serial.println();
    Serial.print("status : ");
    Serial.println(responStatus);
    
    Serial.print("mode : ");
    Serial.println(responMode);
    
    Serial.print("ket : ");
    Serial.println(responKet);
    Serial.println("-------------------");
    Serial.println();

    lcd.clear();
    lcd.print("System Absensi RFID");
    if (responMode == "SCAN"){
      ModeAlat = "SCAN";
      lcd.setCursor(0,1);
      lcd.print(" SCAN Your RFID Card");
    }else if (responMode == "ADD"){
      ModeAlat = "ADD";
      lcd.setCursor(0,1);
      lcd.print(" ADD Your RFID Card");
    }else{
      ModeAlat = "";
      lcd.setCursor(0,2);
      lcd.print(responKet);
    }
  }
  else
  {
    Serial.println("Error in response");
  }

  http.end();

  delay(100);
}

void loop() {
  if (ModeAlat == "SCAN"){
    Serial.println("SCAN RFID CARD");
    if (rfid.isCard()) {
      if (rfid.readCardSerial()) {
          //Serial.println(rfid.serNum.length());
          BEEP(2, 200);

          Serial.println("");
          Serial.println("Card found");
          String RFID = String(rfid.serNum[0],HEX) +"-"+ String(rfid.serNum[1],HEX) +"-"+ String(rfid.serNum[2],HEX) +"-"+ String(rfid.serNum[3],HEX) +"-"+ String(rfid.serNum[4],HEX);

          
          lcd.setCursor(0,2);
          lcd.print("UID:");
          lcd.print(RFID);
          lcd.print(" ");
          Serial.println(RFID);
          Serial.println("");

          String host = hostSCAN;
          host += "rfid=";
          host += RFID;

          HTTPClient http;

          Serial.print("Request Link:");
          Serial.println(host);
          
          http.begin(wifiClient, host);
          
          int httpCode = http.GET();            //Send the GET request
          String payload = http.getString();    //Get the response payload from server
        
          Serial.print("Response Code:"); //200 is OK
          Serial.println(httpCode);       //Print HTTP return code
        
          Serial.print("Returned data from Server:");
          Serial.println(payload);    //Print request response payload
          
          if(httpCode == 200)
          {
            DynamicJsonDocument doc(1024);
          
           // Parse JSON object
            auto error = deserializeJson(doc, payload);
            if (error) {
              Serial.print(F("deserializeJson() failed with code "));
              Serial.println(error.c_str());
              return;
            }
          
            // Decode JSON/Extract values
            String responStatus = doc["status"].as<String>();
            String responKet = doc["ket"].as<String>();

            lcd.setCursor(0,3);
            lcd.print(responKet);
        
            Serial.println();
            Serial.print("status : ");
            Serial.println(responStatus);
            
            Serial.print("ket : ");
            Serial.println(responKet);
            Serial.println("-------------------");
            Serial.println();

            delay(1000);
            lcd.setCursor(0,3);
            lcd.print("                    ");
        }
      }
    }else{
      Serial.println("WAITING RFID CARD");
      lcd.setCursor(0,2);
      lcd.print("Menunggu Kartu RFID ");
    }
    rfid.halt();
    delay(1000);
  }else if (ModeAlat == "ADD"){
    Serial.println("ADD RFID CARD");
    digitalWrite(lampu, HIGH);
    if (rfid.isCard()) {
      if (rfid.readCardSerial()) {
        //   Serial.println(rfid.serNum.length());
          digitalWrite(lampu, LOW);
          BEEP(2, 500);
        //  digitalWrite(lampu, HIGH);
          Serial.println("");
          Serial.println("Card found");
          String RFID = String(rfid.serNum[0],HEX) +"-"+ String(rfid.serNum[1],HEX) +"-"+ String(rfid.serNum[2],HEX) +"-"+ String(rfid.serNum[3],HEX) +"-"+ String(rfid.serNum[4],HEX);
          DateTime now = rtc.now();       //Menampilkan RTC pada variable now

          Serial.print("Tanggal : ");
          Serial.print(now.day());        //Menampilkan Tanggal
          Serial.print("/");
          Serial.print(now.month());      //Menampilkan Bulan
          Serial.print("/");
          Serial.print(now.year());       //Menampilkan Tahun
          Serial.print(" ");
          
          Serial.print("Jam : ");
          Serial.print(now.hour());       //Menampilkan Jam
          Serial.print(":");
          Serial.print(now.minute());     //Menampilkan Menit
          Serial.print(":");
          Serial.print(now.second());     //Menampilkan Detik
          Serial.println();

          lcd.setCursor(0,2);
          lcd.print("UID:");
          lcd.print(RFID);
          lcd.print(" ");
          Serial.println(RFID);
          Serial.println("");

          String host = hostADD;
          host += "?rfid=";
          host += RFID;

          HTTPClient http;

          Serial.print("Request Link:");
          Serial.println(host);
          
          http.begin(wifiClient, host);
          
          int httpCode = http.GET();            //Send the GET request
          String payload = http.getString();    //Get the response payload from server
        
          Serial.print("Response Code:"); //200 is OK
          Serial.println(httpCode);       //Print HTTP return code
        
          Serial.print("Returned data from Server:");
          Serial.println(payload);    //Print request response payload
          
          if(httpCode == 200)
          {
            DynamicJsonDocument doc(1024);
          
           // Parse JSON object
            auto error = deserializeJson(doc, payload);
            if (error) {
              Serial.print(F("deserializeJson() failed with code "));
              Serial.println(error.c_str());
              return;
            }
          
            // Decode JSON/Extract values
            String responStatus = doc["status"].as<String>();
            String responKet = doc["ket"].as<String>();

            lcd.setCursor(0,3);
            lcd.print(responKet);
        
            Serial.println();
            Serial.print("status : ");
            Serial.println(responStatus);
            
            Serial.print("ket : ");
            Serial.println(responKet);
            Serial.println("-------------------");
            Serial.println();
            
            delay(1000);
            lcd.setCursor(0,3);
            lcd.print("                    ");
        }
      }
    }else{
      Serial.println("WAITING RFID CARD");
      lcd.setCursor(0,2);
      lcd.print("Menunggu Kartu RFID");
    }
    rfid.halt();
    delay(1000);
  }else{
    Serial.println("Tidak Mendapatkan MODE ALAT dari server");
    Serial.println("Cek IP Server dan URL");
    Serial.println("Restart NodeMCU");
    lcd.setCursor(0,1);
    lcd.print("MODE ALAT ERROR");
    lcd.setCursor(0,2); 
    Serial.println("Cek IP Server dan URL");
    lcd.setCursor(0,3);
    Serial.println("Restart NodeMCU");
    delay(10000);         
    ModeDevice();
  }
}

// function sound beep = BEEP(how many, delay on in ms, delay off in ms);
void BEEP(byte c, int wait1){
  for(byte b=0; b<c; b++){
    digitalWrite(Buzzer,HIGH);
    delay(wait1);
    digitalWrite(Buzzer,LOW);
//    delay(wait2);
  }
}
